# Fritzing sketch main (saved by Fritzing 0.9.6b)
breadboards: 1

parts:
  DHT11_1 = DHT11 module
  WeMos_D1_R1 = WeMos D1 R2
  Mod1 = KY-019 5V Relay Module [package="Breakout board"]
  J1 = Piezo Speaker

nets:
  VCC: DHT11_1.VCC, WeMos_D1_R1.5V, Mod1.+, Mod1.Common
  GND: DHT11_1.GND, WeMos_D1_R1.GND, Mod1.-, J1.pin1
  N1: DHT11_1.DATA, WeMos_D1_R1.D1/TX
  N2: WeMos_D1_R1.(D6), Mod1.S
  N3: Mod1.NO, J1.pin2

custom parts:
  DHT11 module: https://cdn-learn.adafruit.com/downloads/pdf/dht.pdf DHT11 black pcb module reference by:https://github.com/adafruit/Fritzing-Library/blob/master/parts/DHT11%20Humitidy%20and%20Temperature%20Sensor.fzpz
  WeMos D1 R2: The D1 R2 is a mini wifi board based on the ESP-8266EX.
  KY-019 5V Relay Module: KY-019 5V Relay module, used to control AC circuits. (Special thanks to vanepp for fixing the PCB holes and other errors)
